# Fritzing sketch fritzing (saved by Fritzing 0.9.3b)

parts:
  U1 = NodeMCU V1.0
  C1 = Electrolytic Capacitor [capacitance=1000μF package="1010 [SMD, electrolytic]"]
  NEOPIXEL1 = Neopixel Strip -- Black (30/m)
  R1 = Resistor [tolerance=±5% resistance=220 package="2010 [SMD]"]

nets:
  N1: U1.D1, R1.Pin_0
  3V3: U1.3V3, C1.+, NEOPIXEL1.+5V
  GND: U1.GND, C1.-, NEOPIXEL1.GND
  N2: NEOPIXEL1.Din, R1.Pin_1

notes:
  Plugin in the micro usb cable here
  The resistor is added between the microcontroller's data pin and the data input on the first NeoPixel to prevent voltage spikes that might otherwise damage the first pixel.
  The capacitor is added across the + and - terminals to prevent the initial onrush of current from damaging the pixels. See here for more information.

custom parts:
  NodeMCU V1.0: ESP8266 based NodeMCU
  Neopixel Strip -- Black (30/m): These NeoPixel strips have 30 digitally-addressable pixel LEDs per meter and are very affordable and are only 12.5 mm wide, 10 mm if you remove the strip from the casing.
